// Logisim project robao-cache.circ as structural Verilog: 1 circuit, main circuit main
module main (
  output [31:0] out_1,
  output [31:0] out_2
);

  wire and_1_out, and_2_out, and_3_out, clock_1_out, comparator_1_eq, comparator_2_eq, decoder_1_out0,
       decoder_1_out4, decoder_1_out6, decoder_1_out8, decoder_1_out10, decoder_1_out12, decoder_1_out13,
       decoder_2_out0, decoder_2_out1, not_1_out, not_2_out, not_3_out, not_4_out, not_5_out, not_6_out,
       not_7_out, not_8_out, not_9_out, not_10_out, not_11_out, not_12_out, or_1_out, ram_2_data;
  wire [1:0] rom_1_data_2;
  wire [3:0] counter_2_q;
  wire [7:0] counter_1_q, ram_1_data, ram_3_data;
  wire [7:1] rom_1_data_3;
  wire [8:0] rom_1_data;
  wire [31:0] multiplexer_1_out, multiplexer_3_out, ram_4_data, ram_5_data, ram_6_data, ram_7_data,
       ram_8_data, ram_9_data, ram_10_data, ram_11_data, register_1_q, register_2_q, register_3_q,
       register_4_q;

  LED HIT (.in(or_1_out));
  Clock clock_1 (.out(clock_1_out));
  not not_1 (not_1_out, ram_2_data);
  Comparator comparator_1 (.a(ram_1_data), .b({rom_1_data_3, 1'b1}), .eq(comparator_1_eq));  // open: gt, lt
  or or_1 (or_1_out, comparator_1_eq, comparator_2_eq);
  Comparator comparator_2 (.a({rom_1_data_3, 1'b1}), .b(ram_3_data), .eq(comparator_2_eq));  // open: gt, lt
  not not_2 (not_2_out, or_1_out);
  RAM #(.addrWidth(5), .bus("separate")) ram_1 (
    .addr(rom_1_data[8:4]), .din({rom_1_data_3, 1'b1}), .data(ram_1_data), .str(and_1_out), .clk(clock_1_out));  // open: sel, ld, clr
  and and_1 (and_1_out, not_3_out, decoder_1_out12);
  Counter counter_1 (.count(and_2_out), .Q(counter_1_q), .clk(clock_1_out));  // open: load, D, carry, clr
  and and_2 (and_2_out, or_1_out, decoder_1_out0);
  Decoder #(.select(4), .enable("false")) decoder_1 (
    .out0(decoder_1_out0), .out4(decoder_1_out4), .out6(decoder_1_out6), .out8(decoder_1_out8),
    .out10(decoder_1_out10), .out12(decoder_1_out12), .out13(decoder_1_out13), .sel(counter_2_q));  // open: out1, out2, out3, out5, out7, out9, out11, out14, out15
  Counter #(.width(4), .max('hf)) counter_2 (
    .count(not_2_out), .Q(counter_2_q), .clk(clock_1_out), .clr(decoder_1_out13));  // open: load, D, carry
  RAM #(.addrWidth(5), .dataWidth(1), .bus("separate")) ram_2 (
    .addr(rom_1_data[8:4]), .din(not_1_out), .data(ram_2_data), .str(decoder_1_out12), .clk(clock_1_out),
    .ld(1'b1));  // open: sel, clr
  not not_3 (not_3_out, ram_2_data);
  ROM #(.dataWidth(16)) rom_1 (
    .addr(counter_1_q), .data({rom_1_data_3, rom_1_data[8:4], rom_1_data_2, rom_1_data[1:0]}));  // open: sel
  RAM #(.addrWidth(5), .bus("separate")) ram_3 (
    .addr(rom_1_data[8:4]), .din({rom_1_data_3, 1'b1}), .data(ram_3_data), .str(and_3_out), .clk(clock_1_out));  // open: sel, ld, clr
  and and_3 (and_3_out, ram_2_data, decoder_1_out12);
  Decoder #(.disabled(0)) decoder_2 (
    .out0(decoder_2_out0), .out1(decoder_2_out1), .sel(ram_2_data), .en(decoder_1_out12));
  not not_4 (not_4_out, or_1_out);
  // MP_main main_1: pin names not known; wires that end beside it: {rom_1_data_3, rom_1_data[8:4], rom_1_data_2, rom_1_data[1:0]}, not_4_out, clock_1_out, out_2
  not not_5 (not_5_out, decoder_2_out0);
  not not_6 (not_6_out, decoder_2_out0);
  Register #(.width(32)) register_1 (.D(out_2), .en(decoder_1_out4), .Q(register_1_q), .clk(clock_1_out));  // open: clr
  RAM #(.addrWidth(5), .dataWidth(32), .bus("separate")) ram_4 (
    .addr(rom_1_data[8:4]), .din(register_1_q), .data(ram_4_data), .str(decoder_2_out0), .clk(clock_1_out),
    .ld(not_5_out));  // open: sel, clr
  RAM #(.addrWidth(5), .dataWidth(32), .bus("separate")) ram_5 (
    .addr(rom_1_data[8:4]), .din(register_3_q), .data(ram_5_data), .str(decoder_2_out0), .clk(clock_1_out),
    .ld(not_6_out));  // open: sel, clr
  Register #(.width(32)) register_2 (.D(out_2), .en(decoder_1_out6), .Q(register_2_q), .clk(clock_1_out));  // open: clr
  not not_7 (not_7_out, decoder_2_out0);
  not not_8 (not_8_out, decoder_2_out0);
  Register #(.width(32)) register_3 (.D(out_2), .en(decoder_1_out8), .Q(register_3_q), .clk(clock_1_out));  // open: clr
  RAM #(.addrWidth(5), .dataWidth(32), .bus("separate")) ram_6 (
    .addr(rom_1_data[8:4]), .din(register_2_q), .data(ram_6_data), .str(decoder_2_out0), .clk(clock_1_out),
    .ld(not_7_out));  // open: sel, clr
  RAM #(.addrWidth(5), .dataWidth(32), .bus("separate")) ram_7 (
    .addr(rom_1_data[8:4]), .din(register_4_q), .data(ram_7_data), .str(decoder_2_out0), .clk(clock_1_out),
    .ld(not_8_out));  // open: sel, clr
  Register #(.width(32)) register_4 (
    .D(out_2), .en(decoder_1_out10), .Q(register_4_q), .clk(clock_1_out));  // open: clr
  Multiplexer #(.select(2), .width(32), .enable("false")) multiplexer_1 (
    .in0(ram_4_data), .in1(ram_6_data), .in2(ram_5_data), .in3(ram_7_data), .out(multiplexer_1_out),
    .sel(rom_1_data_2));
  RAM #(.addrWidth(5), .dataWidth(32), .bus("separate")) ram_8 (
    .addr(rom_1_data[8:4]), .din(register_1_q), .data(ram_8_data), .str(decoder_2_out1), .clk(clock_1_out),
    .ld(not_9_out));  // open: sel, clr
  not not_9 (not_9_out, decoder_2_out1);
  RAM #(.addrWidth(5), .dataWidth(32), .bus("separate")) ram_9 (
    .addr(rom_1_data[8:4]), .din(register_3_q), .data(ram_9_data), .str(decoder_2_out1), .clk(clock_1_out),
    .ld(not_10_out));  // open: sel, clr
  not not_10 (not_10_out, decoder_2_out1);
  Multiplexer #(.width(32), .enable("false")) multiplexer_2 (
    .in0(multiplexer_1_out), .in1(multiplexer_3_out), .out(out_1), .sel(comparator_2_eq));
  not not_11 (not_11_out, decoder_2_out1);
  not not_12 (not_12_out, decoder_2_out1);
  RAM #(.addrWidth(5), .dataWidth(32), .bus("separate")) ram_10 (
    .addr(rom_1_data[8:4]), .din(register_2_q), .data(ram_10_data), .str(decoder_2_out1), .clk(clock_1_out),
    .ld(not_11_out));  // open: sel, clr
  RAM #(.addrWidth(5), .dataWidth(32), .bus("separate")) ram_11 (
    .addr(rom_1_data[8:4]), .din(register_4_q), .data(ram_11_data), .str(decoder_2_out1), .clk(clock_1_out),
    .ld(not_12_out));  // open: sel, clr
  Multiplexer #(.select(2), .width(32), .enable("false")) multiplexer_3 (
    .in0(ram_8_data), .in1(ram_10_data), .in2(ram_9_data), .in3(ram_11_data), .out(multiplexer_3_out),
    .sel(rom_1_data_2));

  // Notes on the sheet:
  //   RESET NOT AVAILABLE :( USE CTRL+R
  //   VIAS
  //   KEYWORD
  //   contents of rom_1 (hex, n*v repeats v):
  //   b804 b004 a004 a000 a050 b050 f050 f058 8800 808 1808 804
  //   UNITED CONTROL
  //   CACHE
endmodule
